# Fritzing sketch Fritzing Sketch Source File (saved by Fritzing 0.9.3b)

parts:
  Part1 = Arduino Uno (Rev3)
  Part2 = HC-SR501 Body Sensor Module
  J1 = Piezo Speaker
  U1 = SWITCH-SPST-2 [package=r_sw_th]
  BAT1 = BC9VPC [package=bc9vpc]
  R2 = Resistor [tolerance=±5% resistance=220 package="2512 [SMD]"]
  LED1 = smd LED [color="Red (633nm)" package="0603 [SMD]"]
  R3 = Resistor [tolerance=±5% resistance=220 package="2512 [SMD]"]
  LED3 = smd LED [color="Red (633nm)" package="0603 [SMD]"]

nets:
  GND: Part1.GND, Part2.GND, J1.pin1, BAT1.V-, LED1.cathode, LED3.cathode
  N1: Part1.D3_PWM, Part2.OUT
  N2: Part1.D4, LED1.anode, R3.Pin_0
  N3: Part1.D5_PWM, R2.Pin_0, LED3.anode
  N4: Part1.D7, J1.pin2
  5V: Part1.5V, Part2.VCC
  N5: Part1.VIN, U1.O
  N6: U1.P, BAT1.V+

notes:
  GND - Black Wire
  5VC - Red Wire
  GPIO - Blue Or Grey Wire
  Intruder Alarm System Using PIR Motion Sensor
  ---- Graphical Diagram ----
  Intruder Alarm System Using PIR Motion Sensor
  ---- Circuit Diagram ----

custom parts:
  HC-SR501 Body Sensor Module: Pyroelectric Infrared PIR Motion Sensor Detector Module
